// Logisim project U.shifter.circ as structural Verilog: 1 circuit, main circuit main
module main (
  input  CLEAR,
  input  S1,
  input  S2,
  input  SINL,
  input  SINR,
  input  in_6,
  input  in_7,
  input  in_8,
  input  in_9,
  output out_10,
  output out_11,
  output out_12,
  output out_13
);

  wire CLK_out, multiplexer_1_out, multiplexer_2_out, multiplexer_3_out, multiplexer_4_out;

  Clock CLK (.out(CLK_out));
  D_Flip_Flop d_ff_1 (.D(multiplexer_1_out), .clk(CLK_out), .Q(out_10), .reset(CLEAR));  // open: Qn, preset
  Multiplexer #(.select(2)) multiplexer_1 (
    .in0(out_10), .in1(SINR), .in2(out_11), .in3(in_7), .out(multiplexer_1_out), .sel({S2, S1}));
  D_Flip_Flop d_ff_2 (.D(multiplexer_2_out), .clk(CLK_out), .Q(out_11), .reset(CLEAR));  // open: Qn, preset
  Multiplexer #(.select(2)) multiplexer_2 (
    .in0(out_11), .in1(out_10), .in2(out_12), .in3(in_8), .out(multiplexer_2_out), .sel({S2, S1}));
  D_Flip_Flop d_ff_3 (.D(multiplexer_3_out), .clk(CLK_out), .Q(out_12), .reset(CLEAR));  // open: Qn, preset
  Multiplexer #(.select(2)) multiplexer_3 (
    .in0(out_12), .in1(out_11), .in3(in_9), .out(multiplexer_3_out), .sel({S2, S1}));  // open: in2
  D_Flip_Flop d_ff_4 (.D(multiplexer_4_out), .clk(CLK_out), .Q(out_13), .reset(CLEAR));  // open: Qn, preset
  Multiplexer #(.select(2)) multiplexer_4 (
    .in0(out_13), .in1(out_12), .in2(SINL), .in3(in_6), .out(multiplexer_4_out), .sel({S2, S1}));
endmodule
